# Fritzing sketch pi_hat_circuit (saved by Fritzing 0.9.3b)

parts:
  Part1 = Adafruit Perma-Proto HAT [part_number="Adafruit #2314 and #2310"]
  Q6 = NPN-Transistor [package="TO92 [THT]"]
  R10 = Resistor [tolerance=±20% resistance=270 package=THT]
  R11 = Resistor [tolerance=±20% resistance=270 package=THT]
  R12 = Resistor [tolerance=±5% resistance=220 package=THT]
  R13 = Resistor [tolerance=±5% resistance=220 package=THT]
  Q7 = NPN-Transistor [package="TO92 [THT]"]
  R14 = Resistor [tolerance=±5% resistance=220 package=THT]
  R15 = Resistor [tolerance=±20% resistance=270 package=THT]
  Q8 = NPN-Transistor [package="TO92 [THT]"]
  C2 = Electrolytic Capacitor [capacitance=1µF package="100 mil [THT, electrolytic]"]
  D2 = Diode [package=diode-1n4148]
  Q9 = NPN-Transistor [package="TO92 [THT]"]
  LED2 = LED - 5mm [color="White (4500K)" package="5 mm [THT]"]
  R16 = Resistor [tolerance=±5% resistance=1k package=THT]
  J6 = female pin header, 2 pins [form="♀ (female)"]
  J7 = female pin header, 2 pins [form="♀ (female)"]
  J8 = female pin header, 2 pins [form="♀ (female)"]
  L2 = Solenoid
  S6 = Square Pushbutton
  R17 = Resistor [tolerance=±20% resistance=3.9k package=THT]

nets:
  N1: Part1.GPIO4, Part1.N$61#371
  N2: Part1.GPIO18, R14.Pin_0
  N3: Part1.GPIO23, R13.Pin_0
  N4: Part1.GPIO6, R12.Pin_0
  N5: Part1.GPIO13, R17.Pin_0
  N6: Part1.GPIO20, R16.Pin_0
  N7: Part1.GND, Part1.N$39#266, Part1.N$45#291, Part1.N$62#376, R10.Pin_0, R11.Pin_0, R15.Pin_0, C2.-
  N8: Part1.3.3V, Part1.N$42#276, C2.+, D2.C
  N9: Part1.N$39#270, LED2.anode, J7.pin2
  N10: Part1.N$41#271, R16.Pin_1
  N11: Part1.N$41#275, LED2.cathode, J7.pin1
  N12: Part1.N$42#280, J8.pin2, L2.pin2
  N13: Part1.N$43#282, D2.A
  N14: Part1.N$43#283, Q9.C
  N15: Part1.N$43#285, J8.pin1, L2.pin1
  N16: Part1.N$44#286, R17.Pin_1
  N17: Part1.N$44#288, Q9.B
  N18: Part1.N$45#293, Q9.E
  N19: Part1.N$46#296, R12.Pin_1
  N20: Part1.N$46#300, Q8.C
  N21: Part1.N$47#305, Q8.B
  N22: Part1.N$48#309, R11.Pin_1
  N23: Part1.N$48#310, Q8.E
  N24: Part1.N$55#341, R13.Pin_1
  N25: Part1.N$55#344, Q6.C
  N26: Part1.N$56#350, Q6.B
  N27: Part1.N$57#354, R10.Pin_1
  N28: Part1.N$57#355, Q6.E
  N29: Part1.N$58#356, R14.Pin_1
  N30: Part1.N$58#360, Q7.C
  N31: Part1.N$59#364, R15.Pin_1
  N32: Part1.N$59#365, Q7.E
  N33: Part1.N$60#370, Q7.B
  N34: Part1.N$61#373, J6.pin2, S6.leg1
  N35: Part1.N$62#378, J6.pin1, S6.leg0

custom parts:
  Adafruit Perma-Proto HAT: To kick off the Adafruit HAT party, we have this Perma-Proto inspired plug in daughter board. It has a grid of 0.1" prototyping soldering holes for attaching chips, resistors, LED, potentiometers and more. The holes are connected underneath with traces to mimic the solderless breadboards you're familiar. There's also long power strips for +3V, +5V and Ground connections to the Pi. Near the top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
