# Fritzing sketch stripboard_circuit (saved by Fritzing 0.9.3b)
stripboards: 1

parts:
  R2 = Resistor [tolerance=±20% resistance=270 package=THT]
  R3 = Resistor [tolerance=±5% resistance=220 package=THT]
  Q2 = NPN-Transistor [package="TO92 [THT]"]
  R4 = Resistor [tolerance=±20% resistance=270 package=THT]
  R5 = Resistor [tolerance=±5% resistance=220 package=THT]
  R6 = Resistor [tolerance=±5% resistance=220 package=THT]
  R7 = Resistor [tolerance=±20% resistance=270 package=THT]
  Q3 = NPN-Transistor [package="TO92 [THT]"]
  Q4 = NPN-Transistor [package="TO92 [THT]"]
  C1 = Electrolytic Capacitor [capacitance=1µF package="100 mil [THT, electrolytic]"]
  Q5 = NPN-Transistor [package="TO92 [THT]"]
  D1 = Diode [package=diode-1n4148]
  LED1 = LED - 5mm [color="White (4500K)" package="5 mm [THT]"]
  R9 = Resistor [tolerance=±5% resistance=1k package=THT]
  J1 = female pin header, 2 pins [form="♀ (female)"]  # not connected
  L1 = Solenoid  # not connected
  S5 = Square Pushbutton
  R8 = Resistor [tolerance=±20% resistance=3.9k package=THT]
  J2 = double row female pin header, 4 pins [form="♀ (female)"]
  J3 = double row female pin header, 4 pins [form="♀ (female)"]

nets:
  N1: R2.Pin_0, R2.Pin_1, Q2.E, R4.Pin_0, R4.Pin_1, R7.Pin_0, R7.Pin_1, Q3.E, Q4.E, C1.-, Q5.E, LED1.anode, S5.leg0, S5.leg1, J2.pin1, J3.pin1
  N2: R3.Pin_0, R3.Pin_1, Q3.C, J2.pin2
  N3: Q2.C, R5.Pin_0, R5.Pin_1, R6.Pin_0, R6.Pin_1, Q4.C, J2.pin3, J2.pin4
  N4: C1.+, Q5.C, D1.A
  N5: Q5.B, R8.Pin_0, R8.Pin_1, J3.pin3
  N6: LED1.cathode, R9.Pin_0, R9.Pin_1, J3.pin2
